# Fritzing sketch SchemaElec (saved by Fritzing 0.9.3b)
breadboards: 1

parts:
  Composant1 = Arduino Uno (Rev3)
  R1 = Resistor [tolerance=±5% resistance=100 package=THT]
  R2 = Resistor [tolerance=±5% resistance=1M package=THT]

nets:
  N1: Composant1.A0, R1.Pin_0, R2.Pin_0
  N2: Composant1.D9_PWM, R1.Pin_1
  GND: Composant1.GND, R2.Pin_1
